# Fritzing sketch Fritzing Circuit Example (saved by Fritzing 0.9.4)
circuit board: 8.46667cm x 5.64444cm

parts:
  WeMos_D1_Mini1 = WeMos D1 Mini
  DS1 = DS18B20 1-Wire Temperature Sensor [part_number=DS18B20]
  R1 = Resistor [tolerance=±5% resistance=4.7k package="2512 [SMD]"]
  R2 = Resistor [tolerance=±5% resistance=470 package=THT]
  S1 = Momentary Switch [package=ksa_sealed_tac_switch]
  Q1 = MOSFET-NCHANNEL [part_number="Mosfet\nIRF520" package=to220v]
  R3 = Resistor [tolerance=±5% resistance=100k package="1206 [SMD]"]
  J3 = Screw terminal - 2 pins [part_number="Power Supply" package=THT]
  J2 = screw terminal, 3 pins
  C6 = Electrolytic Capacitor [capacitance=1000μF package="1010 [SMD, electrolytic]"]
  LED2 = smd LED [color="Red (633nm)" package="0805 [SMD]"]
  R4 = Resistor [tolerance=±5% resistance=220 package="1206 [SMD]"]
  IR1 = tl1838 [part_number=VS1838B package=THT]
  R5 = Photocell (LDR) [package=THT]
  R6 = Resistor [tolerance=±5% resistance=100k package=THT]
  WS2812b_Stripe = Neopixel Strip -- Black (30/m) [part_number=1376]
  JACK1 = 2.1mm Barrel Jack with Terminal Block
  J4 = screw terminal, 6 pins
  U1 = 4RelayModule

nets:
  3V3: WeMos_D1_Mini1.3V3, DS1.VDD, R1.Pin_1, IR1.VCC, R5.pin_1
  5V: WeMos_D1_Mini1.5V, J3.pin2, J2.pin1, C6.+, WS2812b_Stripe.+5V, JACK1.POS, J4.pin5, U1.VCC
  N1: WeMos_D1_Mini1.A0, R5.pin_0, R6.Pin_0
  N2: WeMos_D1_Mini1.D0, J4.pin4, U1.IN4
  N3: WeMos_D1_Mini1.D1, J4.pin1, U1.IN1
  N4: WeMos_D1_Mini1.D2, IR1.OUT
  N5: WeMos_D1_Mini1.D3, S1.2
  N6: WeMos_D1_Mini1.D4, R2.Pin_0
  N7: WeMos_D1_Mini1.D5, DS1.DQ, R1.Pin_0
  N8: WeMos_D1_Mini1.D6, Q1.G, R3.Pin_0, R4.Pin_0
  N9: WeMos_D1_Mini1.D7, J4.pin2, U1.IN2
  N10: WeMos_D1_Mini1.D8, J4.pin3, U1.IN3
  GND: WeMos_D1_Mini1.G, DS1.GND, S1.4, Q1.S, R3.Pin_1, J3.pin1, C6.-, LED2.cathode, IR1.GND, R6.Pin_1, JACK1.NEG, J4.pin6, U1.GND
  N11: R2.Pin_1, J2.pin2, WS2812b_Stripe.Din
  N12: Q1.D, J2.pin3, WS2812b_Stripe.GND
  N13: LED2.anode, R4.Pin_1

notes:
  Suggested pin settings for a WEMOS D1
  - D0 (GPIO 16): Relay 4
  - D1 (GPIO 5) : Relay 1
  - D2 (GPIO 4) : IR Remote
  - D3 (GPIO 0) : Button / LED Clock (when used)
  - D4 (GPIO 2) : Data / WS2812b Stripe
  - D5 (GPIO 14): DS18B20 / IF Temperature Mod
  - D6 (GPIO 12): Stripe Power Switch Mosfet
  - D7 (GPIO 13): Relay 2
  - D8 (GPIO 15): Relay 3
  - A0 (ADC0) : Photoresister
  Usermod: Temperatur
  Usermod: Photoresister sensor with MQTT
  Usermod:
  GeoGab-Relays

custom parts:
  tl1838: The TL1838 is a miniaturized receiver for infrared remote control systems. A PIN diode and a preamplifier are assembled on a lead frame, the epoxy package acts as an IR filter. The demodulated output signal can be directly decoded by a microprocessor.
  Neopixel Strip -- Black (30/m): These NeoPixel strips have 30 digitally-addressable pixel LEDs per meter and are very affordable and are only 12.5 mm wide, 10 mm if you remove the strip from the casing.
  4RelayModule: 4 relay arduino module SONGLE SRD05VDC-SL-C
